# Fritzing sketch Outer_Circuit_Final (saved by Fritzing 1.0.5)
breadboards: 1

parts:
  M1 = 7in-display [package=THT]  # not connected
  A1 = Raspberry Pi 5
  S3 = Pushbutton [package="[SMD]"]
  S4 = Momentary Switch [package=ksa_sealed_tac_switch]
  S5 = Momentary Switch [package=ksa_sealed_tac_switch]
  S6 = Momentary Switch [package=ksa_sealed_tac_switch]
  S7 = Momentary Switch [package=ksa_sealed_tac_switch]
  PIR1 = PIR sensor
  RED_LED1 = LED - 5mm [color="Red (635nm)" current=0.030 package="5 mm [THT]"]
  GREEN_LED1 = LED - 5mm [color="Green (565nm)" current=0.030 package="5 mm [THT]"]
  GREEN_R1 = Resistor [tolerance=±5% resistance=220 package="2010 [SMD]"]
  RED_R1 = Resistor [tolerance=±5% resistance=220 package="2010 [SMD]"]

nets:
  5V: A1.5V, A1.Fan-5V, PIR1.VDD
  GND: A1.GND, A1.Fan-GND, S3.Pin_1, S3.Pin_2, S4.2, S5.2, S6.2, S7.2, PIR1.GND, GREEN_R1.Pin_0, RED_R1.Pin_0
  N1: A1.GPIO14, PIR1.SIG
  N2: A1.GPIO9, RED_LED1.anode
  N3: A1.GPIO11, GREEN_LED1.anode
  N4: A1.GPIO5, S3.Pin_3, S3.Pin_4
  N5: A1.GPIO6, S4.4
  N6: A1.GPIO13, S5.4
  N7: A1.GPIO19, S6.4
  N8: A1.GPIO26, S7.4
  N9: RED_LED1.cathode, RED_R1.Pin_1
  N10: GREEN_LED1.cathode, GREEN_R1.Pin_1

custom parts:
  7in-display: 7In tft rgb touch screen display.
  Raspberry Pi 5: The RPi5, a faster version of the awesome Raspberry Pi4B ARM Board with 40 pin gpio.
